// Logisim project LAB5.circ as structural Verilog: 1 circuit, main circuit B
module B (
  input  C0,
  input  [3:0] in_2,
  input  [3:0] in_3,
  output P1,
  output G1,
  output P2,
  output G2,
  output P3,
  output G3,
  output P0,
  output G0,
  output C4,
  output C1,
  output C2,
  output C3,
  output out_16,
  output out_17,
  output out_18,
  output out_19
);

  wire and_1_out, and_3_out, and_4_out, and_6_out, and_7_out, and_8_out, and_11_out, and_12_out, and_13_out,
       and_14_out;

  and and_1 (and_1_out, C0, P0);
  or or_1 (C1, and_1_out, G0);
  xor xor_1 (out_16, C1, P0);
  xor xor_2 (P0, in_2[0], in_3[0]);
  and and_2 (G0, in_2[0], in_3[0]);
  and and_3 (and_3_out, C0, P0, P1);
  and and_4 (and_4_out, G0, P1);
  or or_2 (C2, and_4_out, and_3_out, G1);
  xor xor_3 (P1, in_2[1], in_3[1]);
  xor xor_4 (out_17, P1, C2);
  and and_5 (G1, in_2[1], in_3[1]);
  and and_6 (and_6_out, G1, P2);
  and and_7 (and_7_out, C0, P0, P1, P2);
  xor xor_5 (P2, in_2[2], in_3[2]);
  and and_8 (and_8_out, G0, G1, P2);
  and and_9 (G2, in_2[2], in_3[2]);
  or or_3 (C3, and_6_out, and_8_out, and_7_out, G2);
  xor xor_6 (out_18, P2, C3);
  xor xor_7 (P3, in_2[3], in_3[3]);
  and and_10 (G3, in_2[3], in_3[3]);
  and and_11 (and_11_out, G2, P3);
  and and_12 (and_12_out, P3, P2, G1);
  and and_13 (and_13_out, P3, P2, P1, G0);
  and and_14 (and_14_out, P3, P2, P1, P0, C0);
  xor xor_8 (out_19, P3, C4);
  or or_4 (C4, and_14_out, and_13_out, and_12_out, and_11_out, G3);
endmodule
